// Logisim project branch_comp.circ as structural Verilog: 1 circuit, main circuit branch_comp
module branch_comp (
  input  [31:0] rs1,
  input  [31:0] rs2,
  input  BrUn,
  output BrEq,
  output BrLt
);

  wire BrEq_signed, BrEq_Unsigned, BrLt_signed, BrLt_Unsigned;

  Comparator #(.mode("unsigned"), .width(32)) comparator_1 (
    .a(rs1), .b(rs2), .eq(BrEq_Unsigned), .lt(BrLt_Unsigned));  // open: gt
  Comparator #(.width(32)) comparator_2 (.a(rs1), .b(rs2), .eq(BrEq_signed), .lt(BrLt_signed));  // open: gt
  Multiplexer #(.enable("false")) multiplexer_1 (.in0(BrEq_Unsigned), .in1(BrEq_signed), .out(BrEq), .sel(BrUn));
  Multiplexer #(.enable("false")) multiplexer_2 (.in0(BrLt_Unsigned), .in1(BrLt_signed), .out(BrLt), .sel(BrUn));

  // Notes on the sheet:
  //   INPUTS to your circuit
  //   DON'T CHANGE THE LOCATIONS OF THE INPUTS AND OUTPUTS!
  //   OUTPUT from your circuit
endmodule
