// Logisim project control_logic.circ as structural Verilog: 1 circuit, main circuit control_logic
module control_logic (
  input  [31:0] inst,
  input  BrEq,
  input  BrLt,
  output PCSel,
  output RegWEn,
  output [2:0] ImmSel,
  output BrUn,
  output ASel,
  output BSel,
  output [3:0] ALUSel,
  output MemRW,
  output [1:0] WBSel,
  output CSRSel,
  output CSRWen,
  output Branch,
  output Jump
);

  wire beq_out, blt_out, bltu_out, bne_out, isAuipc, isIType, isJalr, isLui, isLw, isMul, isMulh, isMulhu,
       isRType, isSra, isSub, isUJType, not_1_out, not_2_out, not_3_out, not_4_out, not_5_out, not_6_out,
       not_7_out, not_8_out, not_9_out, not_10_out, not_11_out, not_12_out, not_13_out, not_14_out,
       not_15_out, not_16_out, not_17_out, not_18_out, not_19_out, not_20_out, not_21_out, not_22_out,
       not_23_out, not_24_out, not_25_out, not_26_out, not_27_out, not_28_out, not_29_out, not_30_out,
       not_31_out, not_32_out, not_33_out, not_34_out, not_35_out, not_36_out, not_37_out, not_38_out,
       not_39_out, not_40_out, not_41_out, not_42_out, not_43_out, not_44_out, not_45_out, not_46_out,
       not_47_out, not_48_out, not_49_out, not_50_out, not_51_out, not_52_out, not_53_out, not_54_out,
       or_4_out, or_5_out, or_6_out, WBToALU, WBToPC;
  wire [1:0] multiplexer_9_out;
  wire [3:0] multiplexer_1_out, multiplexer_2_out, multiplexer_3_out, multiplexer_4_out, multiplexer_6_out,
       multiplexer_7_out, RISel;

  not not_1 (not_1_out, inst[6]);
  not not_2 (not_2_out, inst[14]);
  not not_3 (not_3_out, inst[3]);
  not not_4 (not_4_out, inst[2]);
  not not_5 (not_5_out, inst[6]);
  not not_6 (not_6_out, inst[5]);
  and and_1 (isRType, not_1_out, inst[5], inst[4], not_3_out, not_4_out, inst[1], inst[0]);
  not not_7 (not_7_out, inst[13]);
  not not_8 (not_8_out, inst[12]);
  not not_9 (not_9_out, inst[30]);
  and and_2 (isMul, isRType, not_2_out, not_7_out, not_8_out, not_9_out, inst[25]);
  not not_10 (not_10_out, inst[14]);
  not not_11 (not_11_out, inst[13]);
  not not_12 (not_12_out, inst[12]);
  and beq (beq_out, Branch, BrEq, not_10_out, not_11_out, not_12_out);
  not not_13 (not_13_out, inst[3]);
  not not_14 (not_14_out, inst[2]);
  not not_15 (not_15_out, inst[6]);
  not not_16 (not_16_out, inst[5]);
  not not_17 (not_17_out, inst[4]);
  and and_3 (isIType, not_5_out, not_6_out, inst[4], not_13_out, not_14_out, inst[1], inst[0]);
  not not_18 (not_18_out, inst[14]);
  not not_19 (not_19_out, inst[13]);
  not not_20 (not_20_out, inst[12]);
  not not_21 (not_21_out, inst[25]);
  and and_4 (isSub, isRType, not_18_out, not_19_out, not_20_out, inst[30], not_21_out);
  not not_22 (not_22_out, BrEq);
  not not_23 (not_23_out, inst[14]);
  not not_24 (not_24_out, inst[13]);
  and bne (bne_out, Branch, not_22_out, not_23_out, not_24_out, inst[12]);
  not not_25 (not_25_out, inst[3]);
  not not_26 (not_26_out, inst[2]);
  not not_27 (not_27_out, inst[6]);
  not not_28 (not_28_out, inst[4]);
  and and_5 (isLw, not_15_out, not_16_out, not_17_out, not_25_out, not_26_out, inst[1], inst[0]);
  not not_29 (not_29_out, inst[14]);
  not not_30 (not_30_out, inst[13]);
  not not_31 (not_31_out, inst[30]);
  and and_6 (isMulh, isRType, not_29_out, not_30_out, inst[12], not_31_out, inst[25]);
  and blt (blt_out, Branch, BrLt, inst[14], not_37_out, not_38_out);
  or or_1 (PCSel, beq_out, bne_out, blt_out, bltu_out, isUJType, isJalr);
  not not_32 (not_32_out, inst[3]);
  not not_33 (not_33_out, inst[2]);
  not not_34 (not_34_out, inst[4]);
  and and_7 (MemRW, not_27_out, inst[5], not_28_out, not_32_out, not_33_out, inst[1], inst[0]);
  not not_35 (not_35_out, inst[14]);
  not not_36 (not_36_out, inst[30]);
  and and_8 (isMulhu, isRType, not_35_out, inst[13], inst[12], not_36_out, inst[25]);
  not not_37 (not_37_out, inst[13]);
  not not_38 (not_38_out, inst[12]);
  and bltu (bltu_out, Branch, BrLt, inst[14], inst[13], not_45_out);
  not not_39 (not_39_out, inst[3]);
  not not_40 (not_40_out, inst[2]);
  not not_41 (not_41_out, inst[6]);
  not not_42 (not_42_out, inst[5]);
  and and_9 (Branch, inst[6], inst[5], not_34_out, not_39_out, not_40_out, inst[1], inst[0]);
  not not_43 (not_43_out, inst[13]);
  not not_44 (not_44_out, inst[25]);
  and and_10 (isSra, inst[14], not_43_out, inst[12], inst[30], not_44_out);
  not not_45 (not_45_out, inst[12]);
  not not_46 (not_46_out, inst[3]);
  not not_47 (not_47_out, inst[6]);
  and and_11 (isAuipc, not_41_out, not_42_out, inst[4], not_46_out, inst[2], inst[1], inst[0]);
  not not_48 (not_48_out, inst[4]);
  not not_49 (not_49_out, inst[3]);
  and and_12 (isLui, not_47_out, inst[5], inst[4], not_49_out, inst[2], inst[1], inst[0]);
  not not_50 (not_50_out, blt_out);
  not not_51 (not_51_out, inst[4]);
  and and_13 (isUJType, inst[6], inst[5], not_48_out, inst[3], inst[2], inst[1], inst[0]);
  or or_2 (BrUn, not_50_out, bltu_out);
  not not_52 (not_52_out, inst[3]);
  and and_14 (isJalr, inst[6], inst[5], not_51_out, not_52_out, inst[2], inst[1], inst[0]);
  or or_3 (Jump, isJalr, isUJType);
  not not_53 (not_53_out, inst[3]);
  not not_54 (not_54_out, inst[2]);
  and and_15 (CSRSel, inst[6], inst[5], inst[4], not_53_out, not_54_out, inst[1], inst[0]);
  Multiplexer #(.enable("false"), .select(3), .width(4)) multiplexer_1 (
    .in0(4'b0000), .in1(4'b0110), .in2(4'b0111), .in4(4'b0011), .in5(4'b0100), .in6(4'b0010), .in7(4'b0001),
    .out(multiplexer_1_out), .sel(inst[14:12]));  // open: in3
  or or_4 (or_4_out, isRType, isIType);
  Multiplexer #(.enable("false"), .width(4)) multiplexer_2 (
    .in0(multiplexer_1_out), .in1(4'b1010), .out(multiplexer_2_out), .sel(isMul));
  Multiplexer #(.enable("false"), .width(4)) multiplexer_3 (
    .in0(4'b0000), .in1(RISel), .out(multiplexer_3_out), .sel(or_4_out));
  or or_5 (or_5_out, isIType, isLw);
  Priority_Encoder priority_encoder_1 (
    .in0(or_5_out), .in1(MemRW), .in2(Branch), .in3(or_6_out), .in4(isUJType), .out(ImmSel), .en_in(1'b1));  // open: in5, in6, in7, gs, en_out
  or or_6 (or_6_out, isAuipc, isLui);
  Multiplexer #(.enable("false"), .width(4)) multiplexer_4 (
    .in0(multiplexer_2_out), .in1(4'b1011), .out(multiplexer_4_out), .sel(isMulhu));
  Multiplexer #(.enable("false"), .width(4)) multiplexer_5 (
    .in0(multiplexer_3_out), .in1(4'b1100), .out(ALUSel), .sel(Branch));
  Multiplexer #(.enable("false"), .width(4)) multiplexer_6 (
    .in0(multiplexer_4_out), .in1(4'b1100), .out(multiplexer_6_out), .sel(isSub));
  Multiplexer #(.enable("false"), .width(4)) multiplexer_7 (
    .in0(multiplexer_6_out), .in1(4'b1110), .out(multiplexer_7_out), .sel(isMulh));
  Multiplexer #(.enable("false"), .width(4)) multiplexer_8 (
    .in0(multiplexer_7_out), .in1(4'b0101), .out(RISel), .sel(isSra));
  or or_7 (ASel, Branch, isUJType, isAuipc);
  not not_55 (BSel, isRType);
  or or_8 (WBToALU, isRType, isIType, isAuipc, isLui);
  or or_9 (WBToPC, isUJType, isJalr);
  Multiplexer #(.enable("false"), .width(2)) multiplexer_9 (
    .in0(2'b00), .in1(2'b01), .out(multiplexer_9_out), .sel(WBToALU));
  or or_10 (RegWEn, isRType, isIType, isLw, isAuipc, isLui, CSRSel);
  Multiplexer #(.enable("false"), .width(2)) multiplexer_10 (
    .in0(multiplexer_9_out), .in1(2'b10), .out(WBSel), .sel(WBToPC));

  assign CSRWen = 1'b1;

  // Other names for the same wires on the sheet: opcode[6:0] = inst[6:0]; opcode0 = inst[0]; opcode1 = inst[1];
  //   opcode2 = inst[2]; opcode3 = inst[3]; opcode4 = inst[4]; opcode5 = inst[5]; opcode6 = inst[6];
  //   funct3[2:0] = inst[14:12]; funct3_0 = inst[12]; funct3_1 = inst[13]; funct3_2 = inst[14];
  //   funct7[6:0] = inst[31:25]; funct7_0 = inst[25]; funct7_5 = inst[30]; isCsr = CSRSel; isSBType = Branch;
  //   isSType = MemRW

  // Notes on the sheet:
  //   INPUTS to your circuit
  //   DON'T CHANGE THE LOCATIONS OF THE INPUTS AND OUTPUTS!
  //   OUTPUT from your circuit
  //   一级译码
  //   二级译码
  //   产生PCSel
  //   产生BrUn
  //   add
  //   sll
  //   slt
  //   xor
  //   srl
  //   or
  //   and
  //   产生ALUSel
  //   产生MenRW
  //   产生ImmSel
  //   产生ASel
  //   产生BSel
  //   只有R型指令的rs2为寄存器，其他都是imm
  //   产生WBSel
  //   产生RegWEn
  //   Lw ==》WBSel为1
  //   产生CSRSel
  //   产生CSRSel
endmodule
