// Logisim project cpu.circ as structural Verilog: 3 circuits, main circuit cpu
module cpu (
  input  clk,
  input  [31:0] INSTRUCTION,
  input  [31:0] READ_DATA,
  output [31:0] WRITE_ADDRESS,
  output [31:0] PROGRAM_COUNTER,
  output [31:0] ra,
  output [31:0] sp,
  output [31:0] t0,
  output [31:0] t1,
  output [31:0] t2,
  output [31:0] s0,
  output [31:0] s1,
  output [31:0] a0,
  output [31:0] tohost,
  output [3:0] WRITE_ENABLE,
  output [31:0] WRITE_DATA
);

  wire ASel_EX, ASel_ID, ASel_MEM, ASel_WB, BrEq, BrLt, BrUn_EX, BrUn_ID, BrUn_MEM, BrUn_WB, BSel_EX,
       BSel_ID, BSel_MEM, BSel_WB, CSRSel_EX, CSRSel_ID, CSRSel_MEM, CSRSel_WB, CSRWen_EX, CSRWen_ID,
       CSRWen_MEM, CSRWen_WB, MemRW_EX, MemRW_ID, MemRW_MEM, PCSel_EX, PCSel_ID, PCSel_MEM, PCSel_WB,
       RegWEn_EX, RegWEn_ID, RegWEn_MEM, RegWEn_WB;
  wire [1:0] ForwardA, ForwardB, WBSel_EX, WBSel_ID, WBSel_MEM, WBSel_WB;
  wire [2:0] ImmSel, ImmSel_EX, ImmSel_ID, ImmSel_MEM, ImmSel_WB;
  wire [3:0] ALUSel_EX, ALUSel_ID;
  wire [4:0] rd_EX, rd_MEM, rd_WB, rs1_idx_EX, rs2_idx_EX;
  wire [31:0] adder_1_out, adder_2_out, alu_WB, imm, imm_EX, inst_EX, inst_ID, inst_MEM, inst_WB, mem_WB,
       multiplexer_1_out, multiplexer_2_out, multiplexer_3_out, multiplexer_4_out, multiplexer_5_out,
       multiplexer_6_out, multiplexer_7_out, PC_EX, PC_ID, PC_MEM, PC_WB, READ_DATA_Selected, ReadData1,
       ReadData2, Result, rs1_EX, rs2_EX, WriteData;

  Adder #(.width(32)) adder_1 (.a(PROGRAM_COUNTER), .b(32'h4), .out(adder_1_out));  // open: cin, cout
  Multiplexer #(.enable("false"), .width(32)) multiplexer_1 (
    .in0(adder_1_out), .in1(WRITE_ADDRESS), .out(multiplexer_1_out), .sel(PCSel_ID));
  Register #(.width(32)) PC (.D(multiplexer_1_out), .en(1'b1), .clk(clk), .Q(PROGRAM_COUNTER));  // open: clr
  Multiplexer #(.enable("false"), .width(32)) multiplexer_2 (
    .in0(INSTRUCTION), .in1(32'h13), .out(multiplexer_2_out), .sel(PCSel_ID));
  Register #(.width(32)) u_PC_ID (.D(PROGRAM_COUNTER), .en(1'b1), .clk(clk), .Q(PC_ID));  // open: clr
  Register #(.width(32)) u_inst_ID (.D(multiplexer_2_out), .en(1'b1), .clk(clk), .Q(inst_ID));  // open: clr
  control_logic control_logic_1 (
    .inst(inst_ID), .BrEq(BrEq), .BrLt(BrLt), .PCSel(PCSel_ID), .RegWEn(RegWEn_ID), .ImmSel(ImmSel_ID),
    .BrUn(BrUn_ID), .ASel(ASel_ID), .BSel(BSel_ID), .ALUSel(ALUSel_ID), .MemRW(MemRW_ID), .WBSel(WBSel_ID),
    .CSRSel(CSRSel_ID), .CSRWen(CSRWen_ID));
  imm_gen imm_gen_1 (.inst(inst_ID), .ImmSel(ImmSel), .imm(imm));
  regfile regfile_1 (
    .rs1(inst_ID[19:15]), .rs2(inst_ID[24:20]), .rd(rd_WB), .Write_Data(WriteData), .RegWEn(RegWEn_WB),
    .clk(clk), .ra(ra), .sp(sp), .t0(t0), .t1(t1), .t2(t2), .s0(s0), .s1(s1), .a0(a0),
    .Read_Data_1(ReadData1), .Read_Data_2(ReadData2));
  Register #(.width(5)) register_1 (.D(inst_ID[19:15]), .en(1'b1), .clk(clk), .Q(rs1_idx_EX));  // open: clr
  Register #(.width(5)) register_2 (.D(inst_ID[24:20]), .en(1'b1), .clk(clk), .Q(rs2_idx_EX));  // open: clr
  Register #(.width(32)) u_PC_EX (.D(PC_ID), .en(1'b1), .clk(clk), .Q(PC_EX));  // open: clr
  Register #(.width(5)) u_rd_EX (.D(inst_ID[11:7]), .en(1'b1), .clk(clk), .Q(rd_EX));  // open: clr
  Register #(.width(32)) u_RS1_EX (.D(ReadData1), .en(1'b1), .clk(clk), .Q(rs1_EX));  // open: clr
  Register #(.width(32)) u_RS2_EX (.D(ReadData2), .en(1'b1), .clk(clk), .Q(rs2_EX));  // open: clr
  Register #(.width(32)) u_imm_EX (.D(imm), .en(1'b1), .clk(clk), .Q(imm_EX));  // open: clr
  Register #(.width(32)) u_inst_EX (.D(inst_ID), .en(1'b1), .clk(clk), .Q(inst_EX));  // open: clr
  Register #(.width(1)) register_3 (.D(BSel_ID), .en(1'b1), .clk(clk), .Q(BSel_EX));  // open: clr
  Register #(.width(4)) register_4 (.D(ALUSel_ID), .en(1'b1), .clk(clk), .Q(ALUSel_EX));  // open: clr
  Register #(.width(1)) register_5 (.D(MemRW_ID), .en(1'b1), .clk(clk), .Q(MemRW_EX));  // open: clr
  Register #(.width(2)) register_6 (.D(WBSel_ID), .en(1'b1), .clk(clk), .Q(WBSel_EX));  // open: clr
  Register #(.width(1)) register_7 (.D(CSRSel_ID), .en(1'b1), .clk(clk), .Q(CSRSel_EX));  // open: clr
  Register #(.width(1)) register_8 (.D(CSRWen_ID), .en(1'b1), .clk(clk), .Q(CSRWen_EX));  // open: clr
  Register #(.width(1)) u_PCSel_EX (.D(PCSel_ID), .en(1'b1), .clk(clk), .Q(PCSel_EX));  // open: clr
  Register #(.width(1)) u_RegWEn_EX (.D(RegWEn_ID), .en(1'b1), .clk(clk), .Q(RegWEn_EX));  // open: clr
  Register #(.width(3)) u_ImmSel_EX (.D(ImmSel_ID), .en(1'b1), .clk(clk), .Q(ImmSel_EX));  // open: clr
  Register #(.width(1)) u_BrUn_EX (.D(BrUn_ID), .en(1'b1), .clk(clk), .Q(BrUn_EX));  // open: clr
  Register #(.width(1)) u_ASel_EX (.D(ASel_ID), .en(1'b1), .clk(clk), .Q(ASel_EX));  // open: clr
  Multiplexer #(.enable("false"), .select(2), .width(32)) multiplexer_3 (
    .in0(rs1_EX), .in1(WriteData), .in2(WRITE_ADDRESS), .out(multiplexer_3_out), .sel(ForwardA));  // open: in3
  Multiplexer #(.enable("false"), .select(2), .width(32)) multiplexer_4 (
    .in0(rs2_EX), .in1(WriteData), .in2(WRITE_ADDRESS), .out(multiplexer_4_out), .sel(ForwardB));  // open: in3
  Multiplexer #(.enable("false"), .width(32)) multiplexer_5 (
    .in0(multiplexer_3_out), .in1(imm_EX), .out(multiplexer_5_out), .sel(CSRSel_EX));
  Multiplexer #(.enable("false"), .width(32)) multiplexer_6 (
    .in0(multiplexer_3_out), .in1(PC_EX), .out(multiplexer_6_out), .sel(ASel_EX));
  Multiplexer #(.enable("false"), .width(32)) multiplexer_7 (
    .in0(multiplexer_4_out), .in1(imm_EX), .out(multiplexer_7_out), .sel(BSel_EX));
  branch_comp branch_comp_1 (.rs1(rs1_EX), .rs2(rs2_EX), .BrUn(BrUn_EX), .BrEq(BrEq), .BrLt(BrLt));
  Forwarding forwarding_1 (
    .RegWEn_MEM(RegWEn_MEM), .RegWEn_WB(RegWEn_WB), .rd_MEM(rd_MEM), .rd_WB(rd_WB), .rs1_EX(rs1_idx_EX),
    .rs2_EX(rs2_idx_EX), .ForwardA(ForwardA), .ForwardB(ForwardB));
  alu alu_1 (.Result(Result), .A(multiplexer_6_out), .B(multiplexer_7_out), .ALUSel(ALUSel_EX));
  csr csr_1 (.CSR_address(12'h51e), .CSR_din(multiplexer_5_out), .CSR_WE(CSRWen_EX), .clk(clk), .tohost(tohost));
  Register #(.width(1)) register_9 (.D(BSel_EX), .en(1'b1), .clk(clk), .Q(BSel_MEM));  // open: clr
  Register #(.width(1)) register_10 (.D(MemRW_EX), .en(1'b1), .clk(clk), .Q(MemRW_MEM));  // open: clr
  Register #(.width(2)) register_11 (.D(WBSel_EX), .en(1'b1), .clk(clk), .Q(WBSel_MEM));  // open: clr
  Register #(.width(1)) register_12 (.D(CSRSel_EX), .en(1'b1), .clk(clk), .Q(CSRSel_MEM));  // open: clr
  Register #(.width(1)) register_13 (.D(CSRWen_EX), .en(1'b1), .clk(clk), .Q(CSRWen_MEM));  // open: clr
  Register #(.width(1)) register_14 (.D(PCSel_EX), .en(1'b1), .clk(clk), .Q(PCSel_MEM));  // open: clr
  Register #(.width(1)) register_15 (.D(RegWEn_EX), .en(1'b1), .clk(clk), .Q(RegWEn_MEM));  // open: clr
  Register #(.width(3)) register_16 (.D(ImmSel_EX), .en(1'b1), .clk(clk), .Q(ImmSel_MEM));  // open: clr
  Register #(.width(1)) register_17 (.D(BrUn_EX), .en(1'b1), .clk(clk), .Q(BrUn_MEM));  // open: clr
  Register #(.width(1)) register_18 (.D(ASel_EX), .en(1'b1), .clk(clk), .Q(ASel_MEM));  // open: clr
  Register #(.width(5)) register_19 (.D(rd_EX), .en(1'b1), .clk(clk), .Q(rd_MEM));  // open: clr
  Register #(.width(32)) u_PC_MEM (.D(PC_EX), .en(1'b1), .clk(clk), .Q(PC_MEM));  // open: clr
  Register #(.width(32)) alu_MEM (.D(Result), .en(1'b1), .clk(clk), .Q(WRITE_ADDRESS));  // open: clr
  Register #(.width(32)) rs2_MEM (.D(rs2_EX), .en(1'b1), .clk(clk), .Q(WRITE_DATA));  // open: clr
  Register #(.width(32)) u_inst_MEM (.D(inst_EX), .en(1'b1), .clk(clk), .Q(inst_MEM));  // open: clr
  DMEM dmem_1 (
    .Mem_RW(MemRW_MEM), .inst(inst_MEM), .alu_result(WRITE_ADDRESS), .READ_DATA(READ_DATA),
    .WRITE_EN(WRITE_ENABLE), .READ_DATA_Selected(READ_DATA_Selected));
  Register #(.width(5)) register_20 (.D(rd_MEM), .en(1'b1), .clk(clk), .Q(rd_WB));  // open: clr
  Register #(.width(32)) u_PC_WB (.D(PC_MEM), .en(1'b1), .clk(clk), .Q(PC_WB));  // open: clr
  Register #(.width(32)) u_alu_WB (.D(WRITE_ADDRESS), .en(1'b1), .clk(clk), .Q(alu_WB));  // open: clr
  Register #(.width(32)) u_mem_WB (.D(READ_DATA_Selected), .en(1'b1), .clk(clk), .Q(mem_WB));  // open: clr
  Register #(.width(32)) u_inst_WB (.D(inst_MEM), .en(1'b1), .clk(clk), .Q(inst_WB));  // open: clr
  Register #(.width(1)) register_21 (.D(BSel_MEM), .en(1'b1), .clk(clk), .Q(BSel_WB));  // open: clr
  Register #(.width(2)) register_22 (.D(WBSel_MEM), .en(1'b1), .clk(clk), .Q(WBSel_WB));  // open: clr
  Register #(.width(1)) register_23 (.D(CSRSel_MEM), .en(1'b1), .clk(clk), .Q(CSRSel_WB));  // open: clr
  Register #(.width(1)) register_24 (.D(CSRWen_MEM), .en(1'b1), .clk(clk), .Q(CSRWen_WB));  // open: clr
  Register #(.width(1)) register_25 (.D(PCSel_MEM), .en(1'b1), .clk(clk), .Q(PCSel_WB));  // open: clr
  Register #(.width(1)) register_26 (.D(RegWEn_MEM), .en(1'b1), .clk(clk), .Q(RegWEn_WB));  // open: clr
  Register #(.width(3)) register_27 (.D(ImmSel_MEM), .en(1'b1), .clk(clk), .Q(ImmSel_WB));  // open: clr
  Register #(.width(1)) register_28 (.D(BrUn_MEM), .en(1'b1), .clk(clk), .Q(BrUn_WB));  // open: clr
  Register #(.width(1)) register_29 (.D(ASel_MEM), .en(1'b1), .clk(clk), .Q(ASel_WB));  // open: clr
  Adder #(.width(32)) adder_2 (.a(PC_WB), .b(32'h4), .out(adder_2_out));  // open: cin, cout
  Multiplexer #(.enable("false"), .select(2), .width(32)) multiplexer_8 (
    .in0(mem_WB), .in1(alu_WB), .in2(adder_2_out), .in3(imm_EX), .out(WriteData), .sel(WBSel_WB));

  // Other names for the same wires on the sheet: alu_MEM[31:0] = WRITE_ADDRESS; rd[4:0] = inst_ID[11:7];
  //   rs1[4:0] = inst_ID[19:15]; rs2[4:0] = inst_ID[24:20]; rs2_MEM[31:0] = WRITE_DATA

  // Notes on the sheet:
  //   Output to IMEM
  //   IMEM (do **NOT** move this)
  //   Inputs from IMEM
  //   It is OK to move the PC, RegFile, ALU, MEM, Branch Comp, Imm Gen, and Control Logic to wherever is most convenient for you when constructing your CPU, and to delete this text
  //   Inputs/Outputs for testing. Do **NOT** move these.
  //   Outputs To DMEM
  //   DMEM (do **NOT** move this)
  //   Inputs From DMEM
endmodule

module DMEM (
  input  Mem_RW,
  input  [31:0] inst,
  input  [31:0] alu_result,
  input  [31:0] READ_DATA,
  output [3:0] WRITE_EN,
  output [31:0] READ_DATA_Selected
);

  wire is_lb, is_lb_out, is_lh, is_lh_out, is_sb_out, is_sh_out, is_sw_out, isLw, isSType, not_1_out,
       not_2_out, not_3_out, not_4_out, not_5_out, not_6_out, not_7_out, not_8_out, not_9_out, not_10_out,
       not_11_out, not_12_out, not_13_out, not_14_out, not_15_out, not_16_out, not_17_out, not_18_out,
       not_19_out, not_20_out, not_21_out, not_22_out, not_23_out, not_24_out, not_25_out, not_26_out,
       not_27_out, not_28_out, not_29_out, not_30_out, Sel_0001, Sel_0010, Sel_0011, Sel_0100, Sel_1000,
       Sel_1100, Sel_1111;
  wire [31:0] multiplexer_1_out, READ_DATA_8bits, READ_DATA_16bits;

  not not_1 (not_1_out, inst[6]);
  not not_2 (not_2_out, inst[14]);
  not not_3 (not_3_out, inst[13]);
  not not_4 (not_4_out, inst[12]);
  and is_sb (is_sb_out, isSType, not_2_out, not_3_out, not_4_out);
  not not_5 (not_5_out, inst[4]);
  not not_6 (not_6_out, inst[3]);
  not not_7 (not_7_out, inst[2]);
  and and_1 (isSType, not_1_out, inst[5], not_5_out, not_6_out, not_7_out, inst[1], inst[0]);
  not not_8 (not_8_out, inst[14]);
  not not_9 (not_9_out, inst[13]);
  and is_sh (is_sh_out, isSType, not_8_out, not_9_out, inst[12]);
  not not_10 (not_10_out, inst[6]);
  not not_11 (not_11_out, inst[5]);
  not not_12 (not_12_out, inst[4]);
  not not_13 (not_13_out, inst[3]);
  not not_14 (not_14_out, inst[2]);
  and and_2 (isLw, not_10_out, not_11_out, not_12_out, not_13_out, not_14_out, inst[1], inst[0]);
  not not_15 (not_15_out, inst[14]);
  not not_16 (not_16_out, inst[12]);
  and is_sw (is_sw_out, isSType, not_15_out, inst[13], not_16_out);
  not not_17 (not_17_out, inst[14]);
  not not_18 (not_18_out, inst[13]);
  not not_19 (not_19_out, inst[14]);
  and and_3 (is_lh, not_17_out, not_18_out, inst[12]);
  not not_20 (not_20_out, inst[13]);
  not not_21 (not_21_out, inst[12]);
  and and_4 (is_lb, not_19_out, not_20_out, not_21_out);
  not not_22 (not_22_out, alu_result[1]);
  not not_23 (not_23_out, alu_result[0]);
  not not_24 (not_24_out, alu_result[1]);
  not not_25 (not_25_out, alu_result[0]);
  not not_26 (not_26_out, alu_result[0]);
  not not_27 (not_27_out, alu_result[1]);
  not not_28 (not_28_out, alu_result[0]);
  not not_29 (not_29_out, alu_result[1]);
  not not_30 (not_30_out, alu_result[0]);
  and sw (Sel_1111, is_sw_out, not_22_out, not_23_out);
  and sh_h (Sel_0011, is_sh_out, not_24_out, not_25_out);
  and sh_l (Sel_1100, is_sh_out, alu_result[1], not_26_out);
  and sb_0 (Sel_0001, is_sb_out, not_27_out, not_28_out);
  and sb_1 (Sel_0010, is_sb_out, not_29_out, alu_result[0]);
  and sb_2 (Sel_0100, is_sb_out, alu_result[1], not_30_out);
  and sb_3 (Sel_1000, is_sb_out, alu_result[1], alu_result[0]);
  assign WRITE_EN = Mem_RW ? 4'b0000 : 4'bz;  // Controlled_Buffer controlled_buffer_1
  assign WRITE_EN = Sel_0001 ? 4'b0001 : 4'bz;  // Controlled_Buffer controlled_buffer_2
  assign WRITE_EN = Sel_0010 ? 4'b0010 : 4'bz;  // Controlled_Buffer controlled_buffer_3
  assign WRITE_EN = Sel_0011 ? 4'b0011 : 4'bz;  // Controlled_Buffer controlled_buffer_4
  assign WRITE_EN = Sel_0100 ? 4'b0100 : 4'bz;  // Controlled_Buffer controlled_buffer_5
  assign WRITE_EN = Sel_1000 ? 4'b1000 : 4'bz;  // Controlled_Buffer controlled_buffer_6
  assign WRITE_EN = Sel_1100 ? 4'b1100 : 4'bz;  // Controlled_Buffer controlled_buffer_7
  assign WRITE_EN = Sel_1111 ? 4'b1111 : 4'bz;  // Controlled_Buffer controlled_buffer_8
  Multiplexer #(.enable("false"), .width(32)) multiplexer_1 (
    .in0(READ_DATA), .in1(READ_DATA_16bits), .out(multiplexer_1_out), .sel(is_lh_out));
  and u_is_lh (is_lh_out, isLw, is_lh);
  assign READ_DATA_8bits = {{24{READ_DATA[7]}}, READ_DATA[7:0]};  // Bit_Extender bit_extender_1
  assign READ_DATA_16bits = {{16{READ_DATA[15]}}, READ_DATA[15:0]};  // Bit_Extender bit_extender_2
  and u_is_lb (is_lb_out, isLw, is_lb);
  Multiplexer #(.enable("false"), .width(32)) multiplexer_2 (
    .in0(multiplexer_1_out), .in1(READ_DATA_8bits), .out(READ_DATA_Selected), .sel(is_lb_out));

  // Other names for the same wires on the sheet: READ_DATA_32bits[31:0] = READ_DATA; alu_0 = alu_result[0];
  //   alu_1 = alu_result[1]; inst_MEM[31:0] = inst; opcode[6:0] = inst[6:0]; opcode0 = inst[0]; opcode1 = inst[1];
  //   opcode2 = inst[2]; opcode3 = inst[3]; opcode4 = inst[4]; opcode5 = inst[5]; opcode6 = inst[6];
  //   funct3[2:0] = inst[14:12]; funct3_0 = inst[12]; funct3_1 = inst[13]; funct3_2 = inst[14];
  //   funct7[6:0] = inst[31:25]
endmodule

module Forwarding (
  input  RegWEn_MEM,
  input  RegWEn_WB,
  input  [4:0] rd_MEM,
  input  [4:0] rd_WB,
  input  [4:0] rs1_EX,
  input  [4:0] rs2_EX,
  output [1:0] ForwardA,
  output [1:0] ForwardB
);

  wire and_1_out, and_2_out, and_3_out, and_4_out, comparator_1_eq, comparator_2_eq, rd_MEM_Equal_Rs1,
       rd_MEM_Equal_Rs2, rd_MEM_Not_Zero, rd_WB_Equal_Rs1, rd_WB_Equal_Rs2, rd_WB_Not_Zero;

  Comparator #(.width(5)) comparator_1 (.a(rd_MEM), .b({5{1'b0}}), .eq(comparator_1_eq));  // open: gt, lt
  Comparator #(.width(5)) comparator_2 (.a(rd_WB), .b({5{1'b0}}), .eq(comparator_2_eq));  // open: gt, lt
  Comparator #(.width(5)) comparator_3 (.a(rd_MEM), .b(rs1_EX), .eq(rd_MEM_Equal_Rs1));  // open: gt, lt
  Comparator #(.width(5)) comparator_4 (.a(rd_MEM), .b(rs2_EX), .eq(rd_MEM_Equal_Rs2));  // open: gt, lt
  Comparator #(.width(5)) comparator_5 (.a(rd_WB), .b(rs1_EX), .eq(rd_WB_Equal_Rs1));  // open: gt, lt
  Comparator #(.width(5)) comparator_6 (.a(rd_WB), .b(rs2_EX), .eq(rd_WB_Equal_Rs2));  // open: gt, lt
  not not_1 (rd_MEM_Not_Zero, comparator_1_eq);
  not not_2 (rd_WB_Not_Zero, comparator_2_eq);
  and and_1 (and_1_out, RegWEn_WB, rd_WB_Not_Zero, rd_WB_Equal_Rs1);
  and and_2 (and_2_out, RegWEn_MEM, rd_MEM_Not_Zero, rd_MEM_Equal_Rs1);
  and and_3 (and_3_out, RegWEn_WB, rd_WB_Not_Zero, rd_WB_Equal_Rs2);
  and and_4 (and_4_out, RegWEn_MEM, rd_MEM_Not_Zero, rd_MEM_Equal_Rs2);
  Priority_Encoder #(.select(2)) priority_encoder_1 (
    .in1(and_1_out), .in2(and_2_out), .out(ForwardA), .en_in(1'b1));  // open: in0, in3, gs, en_out
  Priority_Encoder #(.select(2)) priority_encoder_2 (
    .in1(and_3_out), .in2(and_4_out), .out(ForwardB), .en_in(1'b1));  // open: in0, in3, gs, en_out

  // Other names for the same wires on the sheet: ForwardSelA[1:0] = ForwardA; ForwardSelB[1:0] = ForwardB
endmodule
